# Fritzing sketch main controler (saved by Fritzing 0.9.3b)

parts:
  U1 = ESP32-38PinWide [part_number=ESP32-38PinWide]
  Water_Level_Sensor1 = Water Level Sensor
  WATER_PUMP1 = water pump/motor  # not connected
  Mod1 = KY-019 5V Relay Module [package="Breakout board"]
  Part1 = Solar Charge Controller [part_number="HGX Series Solar Charge Controller PWM" package=PWM-Model]
  Part2 = Solar Panel [package="Renogy 50 Watts 12 Volt Monocrystalline Bendable Solar Panel"]
  BAT1 = 12 battery [package=battery]

nets:
  N1: U1.GPIO26, Water_Level_Sensor1.SIG
  N2: U1.GPIO27, Mod1.S
  GND: U1.GND, Water_Level_Sensor1.GND, Mod1.-
  VIN: U1.VIN, Water_Level_Sensor1.VCC, Mod1.+
  N3: Mod1.NO, Part1.Connector_3, BAT1.+
  N4: Part1.Connector_1, Part2.Connector_1
  N5: Part1.Connector_2, Part2.Connector_2
  N6: Part1.Connector_4, BAT1.-

custom parts:
  ESP32-38PinWide: Generic 38-Pin ESP32 with wide format (only access to one side of pins on a breadboard) based on Stephen Lilley's HiLetgo ESP-WROOM-32 ESP32 ESP-32S Development Board.
  Water Level Sensor: A water level sensor. This sensor operates at 3V to 5V. The Sig (signal) pin outputs an analogue signal that is in proportion to the amount of water in contact with the sensor.
  water pump/motor: WATER PUMP BY ARDUBLOCKTR
  KY-019 5V Relay Module: KY-019 5V Relay module, used to control AC circuits. (Special thanks to vanepp for fixing the PCB holes and other errors)
  Solar Charge Controller: PWM-Solar Charge Controller
  Solar Panel: Renogy 50 Watts 12 Volt Solar Panel
  12 battery: 12V lead acid type battery, like the Husqvarna YTH2448 12V 35AH battery. The pads in pcb are sized to accomidate up to 14ga wire (as these batterys will deliver high currents.)
