# Fritzing sketch zone (saved by Fritzing 0.9.3b)

parts:
  VALVE1 = Plastic Solenoid Valve
  U1 = ESP32-38PinWide [part_number=ESP32-38PinWide]
  Capacitive_Soil_Moisture_Sensor1 = DFRobot Capacitive Soil Moisture Sensor V1.0 [part_number=SEN0193]
  A1 = yf-s401 flow sensor [package=THT]
  Mod1 = KY-019 5V Relay Module [package="Breakout board"]
  J2 = Camdenboss CTB0158-2 [part_number=CTB0158-2 package=THT]
  J3 = Camdenboss CTB0158-2 [part_number=CTB0158-2 package=THT]
  J4 = Piezo Speaker
  R2 = Resistor [tolerance=±5% resistance=4.7k package="0402 [SMD]"]
  DS1 = DS18B20 1-Wire Temperature Sensor Probe

nets (from the schematic view):
  N1: VALVE1.no_name_yet#1, Mod1.Common
  N2: VALVE1.no_name_yet#2, J2.pin1
  N3: U1.GPIO32, A1.pin3
  N4: U1.GPIO33, Capacitive_Soil_Moisture_Sensor1.A
  N5: U1.GPIO9, R2.Pin_1, DS1.DQ
  N6: U1.GPIO2, J4.pin2
  N7: U1.GPIO4, Mod1.S
  N8: Capacitive_Soil_Moisture_Sensor1.VCC, R2.Pin_0
  N9: Capacitive_Soil_Moisture_Sensor1.GND, A1.pin2, J3.pin1
  N10: A1.pin1, Mod1.+, J3.pin2
  N11: Mod1.-, J4.pin1
  N12: Mod1.NO, J2.pin2

notes:
  12V
  5V

custom parts:
  ESP32-38PinWide: Generic 38-Pin ESP32 with wide format (only access to one side of pins on a breadboard) based on Stephen Lilley's HiLetgo ESP-WROOM-32 ESP32 ESP-32S Development Board.
  DFRobot Capacitive Soil Moisture Sensor V1.0: DFRobot Capacitive Soil Moisture Sensor V1.0 This product measures soil moisture levels by capacitive sensing, rather than resistive sensing like other types of moisture sensor. It is made of a corrosion resistant material giving it a long service life. Insert it into soil and impress your friends with the real-time soil moisture data! The product includes an on-board voltage regulator which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
  yf-s401 flow sensor: Flow sensors sit in line with your water line, and uses a pinwheel sensor to measure how much liquid has moved through it.
  KY-019 5V Relay Module: KY-019 5V Relay module, used to control AC circuits. (Special thanks to vanepp for fixing the PCB holes and other errors)
